# Fritzing sketch wiring (saved by Fritzing 0.9.3b)

parts:
  V1 = DC Power [voltage=12V]  # not connected
  A3 = XIAO ESP32C3-smd
  Power_plug1 = Power plug
  H1 = polarizedheader 4pin 0.156in [package=THT]

nets:
  N1: A3.Pin_2, A3.Pin_21, Power_plug1.VCC
  N2: A3.Pin_11, H1.pin2, H1.pin3
  N3: Power_plug1.GND, H1.pin1

custom parts:
  XIAO ESP32C3-smd: Seeed Studio XIAO ESP32C3 adopts new RISC-V architecture, supporting both Wi-Fi and BLE wireless connectivities.
